# Fritzing sketch midi-blue main (saved by Fritzing 0.9.3b)
breadboards: 2

parts:
  Часть1 = Arduino Uno (Rev3)
  S1 = Pushbutton [package="[THT]"]
  S2 = Pushbutton [package="[THT]"]
  S3 = Pushbutton [package="[THT]"]
  R1 = Resistor [tolerance=±5% resistance=10k package=THT]
  R2 = Resistor [tolerance=±5% resistance=1k package=THT]
  R3 = Resistor [tolerance=±5% resistance=2.2k package=THT]
  DIN1 = DIN-5 jack (MIDI) [package=THT]
  R4 = Rotary Potentiometer (Small) [maximum_resistance=10kΩ package=THT]
  R6 = Rotary Potentiometer (Small) [maximum_resistance=10kΩ package=THT]
  R7 = Resistor [tolerance=±5% resistance=10k package=THT]
  R8 = Resistor [tolerance=±5% resistance=10k package=THT]
  part = Bluetooth HC-05 Macho
  R5 = Rotary Potentiometer (Small) [maximum_resistance=10kΩ package=THT]
  part_2 = Arduino Uno (Rev3)
  R9 = Resistor [tolerance=±5% resistance=2.2k package=THT]
  R11 = Resistor [tolerance=±5% resistance=1k package=THT]
  part_3 = Bluetooth HC-05 Macho
  R12 = Resistor [tolerance=±5% resistance=220 package=THT]
  R13 = Resistor [tolerance=±5% resistance=220 package=THT]

nets:
  N1: Часть1.A0, R6.wiper
  N2: Часть1.A1, R5.wiper
  N3: Часть1.A2, R4.wiper
  GND: Часть1.GND, R1.Pin_0, R3.Pin_1, R4.leg1, R6.leg1, R7.Pin_0, R8.Pin_0, part.GND, R5.leg1
  N4: Часть1.D0/RX, part.TXD
  N5: Часть1.D1/TX, R2.Pin_0
  N6: Часть1.D2, S1.Pin_3, S1.Pin_4, R8.Pin_1
  N7: Часть1.D3_PWM, S2.Pin_3, S2.Pin_4, R7.Pin_1
  N8: Часть1.D4, S3.Pin_3, S3.Pin_4, R1.Pin_1
  5V: Часть1.5V, S1.Pin_1, S1.Pin_2, S2.Pin_1, S2.Pin_2, S3.Pin_1, S3.Pin_2, R4.leg2, R6.leg2, part.VCC, R5.leg2
  N9: R2.Pin_1, R3.Pin_0, part.RXD
  N10: DIN1.5, R13.Pin_0
  GND_2: DIN1.2, part_2.GND, R9.Pin_1, part_3.GND
  N11: DIN1.4, R12.Pin_0
  N12: part_2.D10_PWM/SS, R13.Pin_1
  N13: part_2.D0/RX, part_3.TXD
  N14: part_2.D1/TX, R11.Pin_0
  5V_2: part_2.5V, part_3.VCC, R12.Pin_1
  N15: R9.Pin_0, R11.Pin_1, part_3.RXD
